# Fritzing sketch DIAGRAM (saved by Fritzing 0.9.2b)

parts:
  Orange_Pi_One3 = Orange Pi One [part_number=OPI-ONE]
  Part23 = Arduino Mega 2560 (Rev3)
  R8 = Resistor [tolerance=±5% resistance=22k package=THT]
  R9 = Resistor [tolerance=±5% resistance=22k package=THT]
  LCD2004-I2C4 = LCD2004-I2C
  Part24 = 16-Channel 12-bit PWM Servo Driver - I2C [part_number=815]
  Part25 = SRF05 Ultrasonic Rangefinder
  Part26 = SRF05 Ultrasonic Rangefinder
  Part27 = SRF05 Ultrasonic Rangefinder
  Part28 = SRF05 Ultrasonic Rangefinder
  J16 = Basic Servo
  J17 = Basic Servo
  J18 = Basic Servo
  Load_Cell7 = Load Cell - Red/white/black/green
  Part29 = HX711 Weighing Sensor Module
  U6 = LM2596 step down module
  U7 = LM2596 step down module
  J19 = Power Plug

nets:
  N1: Orange_Pi_One3.GND, Part23.D15/RX3
  N2: Orange_Pi_One3.5V, Part23.D14/TX3
  N3: Part23.D21/SCL, Part23.SCL, LCD2004-I2C4.SCL, Part24.SCL
  N4: Part23.D20/SDA, Part23.SDA, LCD2004-I2C4.SDA, Part24.SDA
  N5: Part23.D12_PWM, Part25.Trig
  N6: Part23.D11_PWM, Part25.Echo
  N7: Part23.D10_PWM, Part28.Trig
  N8: Part23.D9_PWM, Part28.Echo
  N9: Part23.D8_PWM, Part27.Trig
  VCC: Part23.5V, Part25.VCC, Part26.VCC, Part27.VCC, Part28.VCC
  GND: Part23.GND, Part25.GND, Part26.GND, Part27.GND, Part28.GND
  N10: Part23.D2_PWM, R8.Pin_0, R9.Pin_1
  N11: Part23.D3_PWM, Part29.DO/RX
  N12: Part23.D4_PWM, Part29.CK/TX
  N13: Part23.D5_PWM, Part26.Echo
  N14: Part23.D6_PWM, Part26.Trig
  N15: Part23.D7_PWM, Part27.Echo
  N16: Part24.PWM2, J16.pulse
  N17: Part24.PWM1, J17.pulse
  N18: Part24.PWM0, J18.pulse
  N19: Part24.5.0V, J17.vcc
  GND_2: Part24.GND, J18.gnd
  N20: Load_Cell7.wire1, Part29.E+
  N21: Load_Cell7.wire2, Part29.A+
  N22: Load_Cell7.wire3, Part29.E-
  N23: Load_Cell7.wire4, Part29.A-
  N24: U6.IN-, U6.OUT-
  N25: U7.IN-, U7.OUT-, J19.GND
  N26: U7.OUT+, J19.PWR, J19.tip_PWR

custom parts:
  Orange Pi One: It’s an open-source single-board computer. It can run Android 4.4, Ubuntu, Debian, Rasberry Pi Image, as well as the banana pi Image. It uses the AllWinner H3 SoC, and has 512MB DDR3 SDRAM
  LCD2004-I2C: A standard character display with 4x20 characters. Comes in many colors with LCM2004 IIC attached.
  16-Channel 12-bit PWM Servo Driver - I2C: You want to make a cool robot, maybe a hexapod walker, or maybe just a piece of art with a lot of moving parts. Or maybe you want to drive a lot of LEDs with precise PWM output. Using only two pins, control 16 free-running PWM outputs! You can even chain up 62 breakouts to control up to 992 PWM outputs.
  Load Cell - Red/white/black/green: A rectangle load cell/weighting pressure Sensor with four wires - Red, white, black, green. Normally corresponding with E+, E-, A+, A- respectively.
  HX711 Weighing Sensor Module: HX711 is a precision 24-bit analog-to-digital converter (ADC) designed for weigh scales and industrial control applications to interface directly with a bridge sensor.
  LM2596 step down module: LM2596 DC-DC step down power supply module 3 A.
  Power Plug: Power Jack This is the standard 5.5mm barrel plug for power. This part has bendable leads (i.e. wires in the real world) to connect to wall warts or the breadboard in the standard wire end, and hidden connectors on the tip end that will connect when "plugged in" (overlapped with the jack so it appears "plugged in" in breadboard) to the modified coax jack part. Internal busses connect the two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
